# Fritzing sketch Rpi-custom-voice-hat-wiring (saved by Fritzing 0.9.3b)
breadboards: 1

parts:
  Raspberry_Pi_1 = Raspberry Pi 3 [part_number=RPI-3-V1.2]
  Part1 = Adafruit I2S Mic - SPH0645 [part_number="Adafruit #3421"]
  Part2 = Adafruit I2S Mic - SPH0645 [part_number="Adafruit #3421"]
  Part3 = Adafruit MAX98357A I2S 3W Class D Amplifier [part_number="Adafruit #3006"]

nets:
  VDD: Raspberry_Pi_1.3v3, Part1.VDD, Part2.VDD, Part2.SELECT
  N1: Raspberry_Pi_1.GPIO19, Part1.WS, Part2.WS, Part3.LRCLK
  N2: Raspberry_Pi_1.GPIO21, Part3.DIN
  N3: Raspberry_Pi_1.GPIO20, Part1.DATA, Part2.DATA
  GND: Raspberry_Pi_1.GND, Part1.GND, Part1.SELECT, Part2.GND, Part3.GND
  N4: Raspberry_Pi_1.GPIO18, Part1.BCLK, Part2.BCLK, Part3.BCLK
  5V: Raspberry_Pi_1.5V, Part3.VIN

custom parts:
  Adafruit I2S Mic - SPH0645: For many microcontrollers, adding audio input is easy with one of our analog microphone breakouts. But as you get to bigger and better microcontrollers and microcomputers, you'll find that you don't always have an analog input, or maybe you want to avoid the noise that can seep in with an analog mic system. Once you get past 8-bit micros, you will often find an I2S peripheral, that can take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
  Adafruit MAX98357A I2S 3W Class D Amplifier: Listen to this good news - we now have an all in one digital audio amp breakout board that works incredibly well with the Raspberry Pi! If you're looking for an easy and low cost way to get you digital sound files bumpin' then the MAX08357 I2S Amp Breakout is for you. It takes standard I2S digital audio input and, not only decodes it into analog, but also amplifies it directly into a speaker.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
